# Fritzing sketch HermitCrab (saved by Fritzing 0.9.3b)
breadboards: 1

parts:
  Part1 = Arduino Nano (Rev3.0)
  Part2 = Motor Driver 1A Dual TB6612FNG
  DC_Motor_(Yosoo_6/12V_300RPM) = DC Motor
  DC_Motor_(Yosoo_6/12V_300RPM)_2 = DC Motor
  LiPo_7_4 = LIPO-2000mAh [package=lipo-2000]
  ON/OFF = SWITCH-SPST-2 [package=switch-spst-vertical]
  Digital_Proximity_Sensor_(GP2Y0D810Z0F) = Infrared Proximity Sensor
  IR_receiver_(TSOP2438) = TSOP312.., 314.. [package=THT]
  Analog_Reflectance_Sensor_(MR003-007_1)1 = QRE1113 [package=qre1113]
  J1 = Basic Servo
  LED1 = smd LED [color="Blue (505nm)" package="0603 [SMD]"]
  LED2 = smd LED [color="Blue (505nm)" package="0603 [SMD]"]
  R1 = Resistor [tolerance=±1% resistance=147 package="0402 [SMD]"]
  IR2 = TSOP312.., 314.. [package=THT]
  C1 = Electrolytic Capacitor [capacitance=0.47mF voltage=16V package="0405 [SMD, electrolytic]"]
  C2 = Electrolytic Capacitor [capacitance=1µF package="100 mil [THT, electrolytic]"]

nets:
  GND: Part1.GND, Part2.GND, LiPo_7_4.-, Digital_Proximity_Sensor_(GP2Y0D810Z0F).GND, IR_receiver_(TSOP2438).GND, Analog_Reflectance_Sensor_(MR003-007_1)1.K, Analog_Reflectance_Sensor_(MR003-007_1)1.E, J1.gnd, LED1.cathode, LED2.cathode, IR2.GND, C1.-, C2.-
  N1: Part1.D2, R1.Pin_0
  N2: Part1.D4, Digital_Proximity_Sensor_(GP2Y0D810Z0F).Vout
  N3: Part1.D5, Part2.PWMB
  N4: Part1.D6, Part2.PWMA
  N5: Part1.D8, Part2.AIN2
  N6: Part1.D9, Part2.AIN1
  N7: Part1.D10, J1.pulse
  N8: Part1.D11/MOSI, Part2.BIN1
  N9: Part1.D12/MISO, Part2.BIN2
  N10: Part1.VIN, Part2.VM, ON/OFF.P
  VCC: Part1.5V, Part2.VCC, Digital_Proximity_Sensor_(GP2Y0D810Z0F).Vcc, IR_receiver_(TSOP2438).Vs, Analog_Reflectance_Sensor_(MR003-007_1)1.C, J1.vcc, IR2.Vs, C1.+, C2.+
  N11: Part1.A1, Analog_Reflectance_Sensor_(MR003-007_1)1.A
  N12: Part1.D13/SCK, Part2.STBY
  N13: Part2.B01, DC_Motor_(Yosoo_6/12V_300RPM).pin_1
  N14: Part2.B02, DC_Motor_(Yosoo_6/12V_300RPM).pin_2
  N15: Part2.A02, DC_Motor_(Yosoo_6/12V_300RPM)_2.pin_2
  N16: Part2.A01, DC_Motor_(Yosoo_6/12V_300RPM)_2.pin_1
  N17: LiPo_7_4.+, ON/OFF.O
  N18: IR_receiver_(TSOP2438).Data, IR2.Data
  N19: LED1.anode, LED2.anode, R1.Pin_1
