# Fritzing sketch Oyster-schema (saved by Fritzing 0.9.3b)
breadboards: 1

parts:
  Componente1 = Arduino Uno (Rev3) - ICSP
  Q2 = NPN-Transistor [part_number=to-126 package="SOT-23 [SMD]"]
  R1 = Resistor [tolerance=±1% resistance=100 package="0402 [SMD]"]
  R3 = Resistor [tolerance=±1% resistance=100 package="0402 [SMD]"]
  R4 = Resistor [tolerance=±1% resistance=100 package="0402 [SMD]"]
  R5 = Resistor [tolerance=±1% resistance=100 package="0402 [SMD]"]
  R6 = Resistor [tolerance=±1% resistance=100 package="0402 [SMD]"]
  D1 = LTE-302 [package=lte-302]
  D2 = LTE-302 [package=lte-302]
  D3 = LTE-302 [package=lte-302]
  D4 = LTE-302 [package=lte-302]
  hc-sr1 = hc-sr04
  hc-sr2 = hc-sr04
  hc-sr3 = hc-sr04
  U1 = LIPO-1000mAh [package=lipo-1000]
  U2 = SWITCH-SPST-2 [package=r_sw_th]
  U3 = LIPO-1000mAh [package=lipo-1000]
  J1 = Basic Servo
  DFRobot_DFPlayer_Mini1 = DFRobot DFPlayer Mini [part_number=DFR0299]
  SP1 = SPEAKER [package=pcb_mount_speaker]
  R7 = Resistor [tolerance=±1% resistance=1k package="1206 [SMD]"]
  M1 = DC Motor
  SP2 = SPEAKER [package=pcb_mount_speaker]

nets:
  N1: Componente1.5V, R3.Pin_0, R4.Pin_0, R5.Pin_0, R6.Pin_0
  GND: Componente1.GND, D1.C, D2.C, D4.C, hc-sr1.GND, hc-sr2.GND, hc-sr3.GND, U1.-, U3.-, DFRobot_DFPlayer_Mini1.GND-1, M1.pin_2
  N2: Componente1.D9_PWM, J1.pulse
  N3: Componente1.D10_PWM/SS, hc-sr2.Trig
  N4: Componente1.D11_PWM/MOSI, hc-sr2.Echo
  N5: Componente1.D12/MISO, hc-sr3.Trig
  N6: Componente1.D13/SCK, hc-sr3.Echo
  N7: Componente1.D2, R7.Pin_0
  N8: Componente1.D3_PWM, R1.Pin_0
  N9: Componente1.D4, DFRobot_DFPlayer_Mini1.TX
  N10: Componente1.D6_PWM, hc-sr1.Trig
  N11: Componente1.D7, hc-sr1.Echo
  N12: Componente1.VIN, U2.P
  N13: Q2.2, D1.A, D2.A, D3.A, D4.A
  N14: Q2.0, R1.Pin_1
  N15: Q2.1, R3.Pin_1, R4.Pin_1, R5.Pin_1, R6.Pin_1
  VCC: hc-sr1.VCC, hc-sr2.VCC, hc-sr3.VCC, M1.pin_1
  N16: U1.+, U2.O
  VCC_2: U3.+, J1.vcc, DFRobot_DFPlayer_Mini1.VCC
  N17: DFRobot_DFPlayer_Mini1.RX, R7.Pin_1
  N18: DFRobot_DFPlayer_Mini1.SPK_1, SP1.+, SP2.+
  N19: DFRobot_DFPlayer_Mini1.SPK_2, SP1.-, SP2.-
